# Fritzing sketch schema (saved by Fritzing 0.9.3b)

parts:
  Bauteil1 = Adafruit FXOS8700 + FXAS21002 9 DoF Breakout [part_number="Adafruit #3463"]
  Bauteil2 = Adafruit FeatherWing Proto [part_number="Adafruit #2884"]
  Bauteil3 = Adafruit HUZZAH32 ESP32 Feather [part_number="Adafruit #3405"]  # not connected
  Bauteil4 = Adafruit ADS1115 16Bit I2C ADC [part_number="Adafruit #1085"]
  Bauteil5 = Adafruit MMA8451 Accelerometer [part_number="Adafruit #2019"]
  Bauteil6 = 9-DOF Absolute Orientation IMU Fusion Breakout - BNO055
  M1 = BTS7960
  M2 = RioRand LM2596
  M3 = DC Motor
  BAT1 = Battery Holders [package=battery-aa]
  RE1 = Rotary Encoder [package=THT]
  part = Zener Diode [part_number=3V breakdown_voltage=3V package="Melf DO-213 AB [SMD]"]
  part_2 = Resistor [tolerance=±5% resistance=22k package=THT]
  part_3 = Zener Diode [part_number=3V breakdown_voltage=3V package="Melf DO-213 AB [SMD]"]
  TB1 = KF301-2 [part_number=KF301-2 package="screwterminal-5mm 2 position"]
  part_4 = Resistor [tolerance=±5% resistance=22k package=THT]

nets:
  N1: Bauteil1.SDA, Bauteil2.SDA, Bauteil4.SDA, Bauteil5.SDA, Bauteil6.SDA_5V
  N2: Bauteil1.SCL, Bauteil2.SCL, Bauteil4.SCL, Bauteil5.SCL, Bauteil6.SCL_5V
  GND: Bauteil1.GND, Bauteil2.GND, Bauteil4.AIN1, Bauteil4.ADDR, Bauteil4.GND, Bauteil5.GND, Bauteil6.GND, M1.pin8, M2.Pin_4, RE1.EncoderPinB, part.anode, part_3.anode
  VIN: Bauteil1.VIN, Bauteil2.3V, Bauteil5.VIN, Bauteil6.5.0V
  N3: Bauteil2.D, M1.pin1
  N4: Bauteil2.E, M1.pin2
  N5: Bauteil2.F, M1.pin3, M1.pin4
  N6: Bauteil2.H, part_2.Pin_1, part_3.cathode
  N7: Bauteil2.I, part.cathode, part_4.Pin_1
  N8: Bauteil2.USB, Bauteil4.VDD, M1.pin7, M2.Pin_3, RE1.EncoderPinA
  N9: Bauteil4.AIN0, RE1.EncoderPinC
  N10: M1.pin9, M3.pin_2
  N11: M1.pin10, M3.pin_1
  N12: M1.pin11, M2.Pin_1, BAT1.-
  N13: M1.pin12, M2.Pin_2, BAT1.+
  N14: part_2.Pin_0, TB1.2
  N15: TB1.1, part_4.Pin_0

notes:
  Tractor Battery, use the 3pin-connector in the cab for a good connection
  Stack the esp32-feather on top of the protowing
  Setup for 5V or use an UBEC
  Connect GND here
  Use a pairwise drilled cable, pe. a ethernet cable, keep away from high-current lines
  Connect shield here
  Use the actual pinout and supply voltage of the angle sensor
  use either USB or battery supply
  Zener Diodes
  Work and steer switches
  Resistors
  Recomended
  Not recomended
  To F9P RX1
  To F9P TX1

custom parts:
  Adafruit FXOS8700 + FXAS21002 9 DoF Breakout: The NXP Precision 9DoF breakout combines two of the best motion sensors we've tested here at Adafruit: The FXOS8700 3-Axis accelerometer and magnetometer, and the FXAS21002 3-axis gyroscope. These two sensors combine to make a nice 9-DoF kit, that can be used for motion and orientation sensing. In particular, we think this sensor set is ideal for AHRS-based orientation calculations: the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
  Adafruit FeatherWing Proto: This is the FeatherWing Proto - a prototyping add-on for all Feather boards. Using our Feather Stacking Headers or Feather Female Headers you can connect a FeatherWing on top or bottom of your Feather board and let the board take flight! This has a duplicate breakout for each pin on a Feather, as well as a bunch of plain grid proto holes. For GND and 3.3V, we give you a strip of connected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
  Adafruit ADS1115 16Bit I2C ADC: For microcontrollers without an analog-to-digital converter or when you want a higher-precision ADC, the ADS1115 provides 16-bit precision at 860 samples/second over I2C. The chip can be configured as 4 single-ended input channels, or two differential channels. As a nice bonus, it even includes a programmable gain amplifier, up to x16, to help boost up smaller single/differential signals to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
  Adafruit MMA8451 Accelerometer: So many accelerometers and so little time! We've expanded our accelerometer selection even more with this high-precision and inexpensive MMA8451 Triple-Axis Accelerometer w/ 14-bit ADC. You can detect motion, tilt and basic orientation with a digital accelerometer - and the MMA8451 is a great accelerometer to start with. It has a wide usage range, from +-2g up to +-8g yet is easy to use with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
  9-DOF Absolute Orientation IMU Fusion Breakout - BNO055: A MEMS accelerometer, magnetometer and gyroscope on a single die with a high speed ARM Cortex-M0 based processor to digest all the sensor data, abstract the sensor fusion and real time requirements away, and spit out data you can use in quaternions, Euler angles or vectors.
  BTS7960: BTS7960 43A Peak Power H-Bridge PWM Motor Driver
  KF301-2: KF301-3 is a 3 position screw terminal header block with male through hole PCB pins on 5mm spacing
